# Fritzing sketch SensorBoard (saved by Fritzing 0.9.2b)
circuit board: 8.46667cm x 5.64444cm
breadboards: 1

parts:
  R1 = Resistor [tolerance=±5% resistance=220 package=THT]
  J1 = female pin header, 2 pins [form="♀ (female)"]
  J1_2 = female alternating pin header, 2 pins [form="♀ (female)"]
  J1_3 = female pin header, 8 pins [form="♀ (female)"]

nets:
  N1: R1.Pin_0, J1.pin1, J1_2.pin1, J1_3.pin1
  N2: R1.Pin_1, J1.pin2, J1_2.pin2, J1_3.pin2
